// Digital circuit cpu.dig as structural Verilog
module cpu (
  input  Clock,
  input  PC_inc,
  input  PC_r,
  input  PC_w,
  input  IRH_w,
  input  IRL_w,
  input  DIR_sel,
  input  IMM_sel,
  input  Rs_src,
  input  Rd_w,
  input  Rs_r,
  input  IND_sel,
  input  SPC_r,
  input  SPC_w,
  input  RAM_r,
  input  RAM_w,
  output [4:0] out_2
);

  wire instruction_1_p9, instruction_1_p10, instruction_1_p11, instruction_1_p14;
  wire [7:0] ramsingleport_1_d;
  wire [15:0] pc_1_a_out;

  pc pc_1 (.PC_inc(PC_inc), .CLK(Clock), .PC_r(PC_r), .PC_w(PC_w), .A_in(pc_1_a_out), .RST(1'b0), .A_out(pc_1_a_out));
  RAMSinglePort #(.AddrBits(16), .Bits(8)) ramsingleport_1 (
    .A(pc_1_a_out), .str(RAM_w), .C(Clock), .ld(RAM_r), .D(ramsingleport_1_d));
  // instruction instruction_1: pin names not known; wires that end beside it: ramsingleport_1_d, Clock, IRH_w, IRL_w, DIR_sel, IMM_sel, Rs_src, out_2, instruction_1_p9, instruction_1_p10, instruction_1_p11, ramsingleport_1_d, pc_1_a_out, instruction_1_p14
  // registers registers_1: pin names not known; wires that end beside it: pc_1_a_out, ramsingleport_1_d, Clock, instruction_1_p9, Rd_w, instruction_1_p14, instruction_1_p10, Rs_r, instruction_1_p11, DIR_sel, IND_sel, SPC_r, SPC_w, pc_1_a_out, ramsingleport_1_d

  // Other names for the same wires on the sheet: CLK = Clock

  // Notes on the sheet:
  //   Rd_w: Write to destination register
  //   Rs_r: Read from source register
endmodule
